// Logisim project RISCVI Complete DataPath.circ as structural Verilog: 15 circuits, main circuit main
module main (
  input  in_1,
  output [31:0] out_2
);

  wire clock_1_out;
  wire [31:0] adder_1_out, register_1_q;

  Clock clock_1 (.out(clock_1_out));
  Register #(.width(32)) register_1 (.D(adder_1_out), .Q(register_1_q), .clk(clock_1_out), .clr(in_1));  // open: en
  Adder #(.width(32)) adder_1 (.a(32'h4), .b(register_1_q), .out(adder_1_out));  // open: cin, cout
  ROM #(.addrWidth(20), .dataWidth(32)) rom_1 (.addr(register_1_q[21:2]), .data(out_2));  // open: sel

  // Notes on the sheet:
  //   FETCH UNIT
  //   contents of rom_1 (hex, n*v repeats v):
  //   11111111
endmodule

module PC (
  input  in_1,
  output [31:0] out_2
);

  wire clock_1_out;
  wire [31:0] adder_1_out, register_1_q;

  Clock clock_1 (.out(clock_1_out));
  Register #(.width(32)) register_1 (.D(adder_1_out), .Q(register_1_q), .clk(clock_1_out), .clr(in_1));  // open: en
  Adder #(.width(32)) adder_1 (.a(32'h4), .b(register_1_q), .out(adder_1_out));  // open: cin, cout
  ROM #(.addrWidth(20), .dataWidth(32)) rom_1 (.addr(register_1_q[21:2]), .data(out_2));  // open: sel

  // Notes on the sheet:
  //   FETCH UNIT
  //   contents of rom_1 (hex, n*v repeats v):
  //   11111111
endmodule

module Reg_file (
  input  [31:0] in_1,
  input  write_enable,
  input  [4:0] rs1,
  input  [4:0] rd,
  input  [4:0] rs2,
  input  in_6,
  input  in_7,
  output [31:0] out_8,
  output [31:0] out_9
);

  wire decoder_1_out0, decoder_1_out1, decoder_1_out2, decoder_1_out3, decoder_1_out4, decoder_1_out5,
       decoder_1_out6, decoder_1_out7, decoder_1_out8, decoder_1_out9, decoder_1_out10, decoder_1_out11,
       decoder_1_out12, decoder_1_out13, decoder_1_out14, decoder_1_out15, decoder_1_out16, decoder_1_out17,
       decoder_1_out18, decoder_1_out19, decoder_1_out20, decoder_1_out21, decoder_1_out22, decoder_1_out23,
       decoder_1_out24, decoder_1_out25, decoder_1_out26, decoder_1_out27, decoder_1_out28, decoder_1_out29,
       decoder_1_out30, decoder_1_out31;
  wire [31:0] multiplexer_1_out, register_1_q, register_2_q, register_3_q, register_4_q, register_5_q,
       register_6_q, register_7_q, register_8_q, register_9_q, register_10_q, register_11_q, register_12_q,
       register_13_q, register_14_q, register_15_q, register_16_q, register_17_q, register_18_q,
       register_19_q, register_20_q, register_21_q, register_22_q, register_23_q, register_24_q,
       register_25_q, register_26_q, register_27_q, register_28_q, register_29_q, register_30_q,
       register_31_q, register_32_q;

  Decoder #(.select(5)) decoder_1 (
    .out0(decoder_1_out0), .out1(decoder_1_out1), .out2(decoder_1_out2), .out3(decoder_1_out3),
    .out4(decoder_1_out4), .out5(decoder_1_out5), .out6(decoder_1_out6), .out7(decoder_1_out7),
    .out8(decoder_1_out8), .out9(decoder_1_out9), .out10(decoder_1_out10), .out11(decoder_1_out11),
    .out12(decoder_1_out12), .out13(decoder_1_out13), .out14(decoder_1_out14), .out15(decoder_1_out15),
    .out16(decoder_1_out16), .out17(decoder_1_out17), .out18(decoder_1_out18), .out19(decoder_1_out19),
    .out20(decoder_1_out20), .out21(decoder_1_out21), .out22(decoder_1_out22), .out23(decoder_1_out23),
    .out24(decoder_1_out24), .out25(decoder_1_out25), .out26(decoder_1_out26), .out27(decoder_1_out27),
    .out28(decoder_1_out28), .out29(decoder_1_out29), .out30(decoder_1_out30), .out31(decoder_1_out31),
    .sel(rd), .en(write_enable));
  Multiplexer #(.width(32), .enable("false")) multiplexer_1 (
    .in1(in_1), .out(multiplexer_1_out), .sel(write_enable));  // open: in0
  Register #(.width(32)) register_1 (.D({32{1'b0}}), .en(decoder_1_out0), .Q(register_1_q), .clk(in_6), .clr(in_7));
  Register #(.width(32)) register_2 (
    .D(multiplexer_1_out), .en(decoder_1_out2), .Q(register_2_q), .clk(in_6), .clr(in_7));
  Register #(.width(32)) register_3 (
    .D(multiplexer_1_out), .en(decoder_1_out4), .Q(register_3_q), .clk(in_6), .clr(in_7));
  Register #(.width(32)) register_4 (
    .D(multiplexer_1_out), .en(decoder_1_out6), .Q(register_4_q), .clk(in_6), .clr(in_7));
  Register #(.width(32)) register_5 (
    .D(multiplexer_1_out), .en(decoder_1_out8), .Q(register_5_q), .clk(in_6), .clr(in_7));
  Register #(.width(32)) register_6 (
    .D(multiplexer_1_out), .en(decoder_1_out10), .Q(register_6_q), .clk(in_6), .clr(in_7));
  Register #(.width(32)) register_7 (
    .D(multiplexer_1_out), .en(decoder_1_out12), .Q(register_7_q), .clk(in_6), .clr(in_7));
  Register #(.width(32)) register_8 (
    .D(multiplexer_1_out), .en(decoder_1_out14), .Q(register_8_q), .clk(in_6), .clr(in_7));
  Register #(.width(32)) register_9 (
    .D(multiplexer_1_out), .en(decoder_1_out16), .Q(register_9_q), .clk(in_6), .clr(in_7));
  Register #(.width(32)) register_10 (
    .D(multiplexer_1_out), .en(decoder_1_out18), .Q(register_10_q), .clk(in_6), .clr(in_7));
  Register #(.width(32)) register_11 (
    .D(multiplexer_1_out), .en(decoder_1_out20), .Q(register_11_q), .clk(in_6), .clr(in_7));
  Register #(.width(32)) register_12 (
    .D(multiplexer_1_out), .en(decoder_1_out22), .Q(register_12_q), .clk(in_6), .clr(in_7));
  Register #(.width(32)) register_13 (
    .D(multiplexer_1_out), .en(decoder_1_out24), .Q(register_13_q), .clk(in_6), .clr(in_7));
  Register #(.width(32)) register_14 (
    .D(multiplexer_1_out), .en(decoder_1_out26), .Q(register_14_q), .clk(in_6), .clr(in_7));
  Register #(.width(32)) register_15 (
    .D(multiplexer_1_out), .en(decoder_1_out28), .Q(register_15_q), .clk(in_6), .clr(in_7));
  Register #(.width(32)) register_16 (
    .D(multiplexer_1_out), .en(decoder_1_out30), .Q(register_16_q), .clk(in_6), .clr(in_7));
  Register #(.width(32)) register_17 (
    .D(multiplexer_1_out), .en(decoder_1_out1), .Q(register_17_q), .clk(in_6), .clr(in_7));
  Register #(.width(32)) register_18 (
    .D(multiplexer_1_out), .en(decoder_1_out3), .Q(register_18_q), .clk(in_6), .clr(in_7));
  Register #(.width(32)) register_19 (
    .D(multiplexer_1_out), .en(decoder_1_out5), .Q(register_19_q), .clk(in_6), .clr(in_7));
  Register #(.width(32)) register_20 (
    .D(multiplexer_1_out), .en(decoder_1_out7), .Q(register_20_q), .clk(in_6), .clr(in_7));
  Register #(.width(32)) register_21 (
    .D(multiplexer_1_out), .en(decoder_1_out9), .Q(register_21_q), .clk(in_6), .clr(in_7));
  Register #(.width(32)) register_22 (
    .D(multiplexer_1_out), .en(decoder_1_out11), .Q(register_22_q), .clk(in_6), .clr(in_7));
  Register #(.width(32)) register_23 (
    .D(multiplexer_1_out), .en(decoder_1_out13), .Q(register_23_q), .clk(in_6), .clr(in_7));
  Register #(.width(32)) register_24 (
    .D(multiplexer_1_out), .en(decoder_1_out15), .Q(register_24_q), .clk(in_6), .clr(in_7));
  Register #(.width(32)) register_25 (
    .D(multiplexer_1_out), .en(decoder_1_out17), .Q(register_25_q), .clk(in_6), .clr(in_7));
  Register #(.width(32)) register_26 (
    .D(multiplexer_1_out), .en(decoder_1_out19), .Q(register_26_q), .clk(in_6), .clr(in_7));
  Register #(.width(32)) register_27 (
    .D(multiplexer_1_out), .en(decoder_1_out21), .Q(register_27_q), .clk(in_6), .clr(in_7));
  Register #(.width(32)) register_28 (
    .D(multiplexer_1_out), .en(decoder_1_out23), .Q(register_28_q), .clk(in_6), .clr(in_7));
  Register #(.width(32)) register_29 (
    .D(multiplexer_1_out), .en(decoder_1_out25), .Q(register_29_q), .clk(in_6), .clr(in_7));
  Register #(.width(32)) register_30 (
    .D(multiplexer_1_out), .en(decoder_1_out27), .Q(register_30_q), .clk(in_6), .clr(in_7));
  Register #(.width(32)) register_31 (
    .D(multiplexer_1_out), .en(decoder_1_out29), .Q(register_31_q), .clk(in_6), .clr(in_7));
  Register #(.width(32)) register_32 (
    .D(multiplexer_1_out), .en(decoder_1_out31), .Q(register_32_q), .clk(in_6), .clr(in_7));
  Multiplexer #(.select(5), .width(32)) multiplexer_2 (
    .in0(register_1_q), .in1(register_17_q), .in2(register_2_q), .in3(register_18_q), .in4(register_3_q),
    .in5(register_19_q), .in6(register_4_q), .in7(register_20_q), .in8(register_5_q), .in9(register_21_q),
    .in10(register_6_q), .in11(register_22_q), .in12(register_7_q), .in13(register_23_q),
    .in14(register_8_q), .in15(register_24_q), .in16(register_9_q), .in17(register_25_q),
    .in18(register_10_q), .in19(register_26_q), .in20(register_11_q), .in21(register_27_q),
    .in22(register_12_q), .in23(register_28_q), .in24(register_13_q), .in25(register_29_q),
    .in26(register_14_q), .in27(register_30_q), .in28(register_15_q), .in29(register_31_q),
    .in30(register_16_q), .in31(register_32_q), .out(out_8), .sel(rs1));  // open: en
  Multiplexer #(.select(5), .width(32)) multiplexer_3 (
    .in0(register_1_q), .in1(register_17_q), .in2(register_2_q), .in3(register_18_q), .in4(register_3_q),
    .in5(register_19_q), .in6(register_4_q), .in7(register_20_q), .in8(register_5_q), .in9(register_21_q),
    .in10(register_6_q), .in11(register_22_q), .in12(register_7_q), .in13(register_23_q),
    .in14(register_8_q), .in15(register_24_q), .in16(register_9_q), .in17(register_25_q),
    .in18(register_10_q), .in19(register_26_q), .in20(register_11_q), .in21(register_27_q),
    .in22(register_12_q), .in23(register_28_q), .in24(register_13_q), .in25(register_29_q),
    .in26(register_14_q), .in27(register_30_q), .in28(register_15_q), .in29(register_31_q),
    .in30(register_16_q), .in31(register_32_q), .out(out_9), .sel(rs2));  // open: en

  // Notes on the sheet:
  //   data
endmodule

module Imediate_generator (
  input  [31:0] in_1,
  input  [31:0] PC,
  output [31:0] out_3,
  output [31:0] out_4,
  output [31:0] out_5,
  output [31:0] out_6,
  output [31:0] out_7,
  output [31:0] out_8,
  output [31:0] out_9
);

  wire [31:0] bit_extender_3_out, bit_extender_4_out, bit_extender_5_out, bit_extender_6_out, shifter_2_out;

  assign out_3 = {{20{in_1[31]}}, in_1[31:20]};  // Bit_Extender bit_extender_1
  assign out_4 = {{20{in_1[31]}}, {in_1[31:25], in_1[11:7]}};  // Bit_Extender bit_extender_2
  assign bit_extender_3_out = {{19{in_1[31]}}, {in_1[31], in_1[7], in_1[30:25], in_1[11:8], 1'b0}};  // Bit_Extender bit_extender_3
  assign bit_extender_4_out = {{12{in_1[31]}}, in_1[31:12]};  // Bit_Extender bit_extender_4
  Shifter #(.width(32)) shifter_1 (.in(bit_extender_4_out), .\dist (5'b01100), .out(out_6));
  assign bit_extender_5_out = {{12{in_1[31]}}, in_1[31:12]};  // Bit_Extender bit_extender_5
  Shifter #(.width(32)) shifter_2 (.in(bit_extender_5_out), .\dist (5'b01100), .out(shifter_2_out));
  assign bit_extender_6_out = {{11{in_1[31]}}, {in_1[31], in_1[19:12], in_1[20], in_1[30:21], 1'b0}};  // Bit_Extender bit_extender_6
  Adder #(.width(32)) adder_1 (.a(PC), .b(bit_extender_3_out), .out(out_5));  // open: cin, cout
  Adder #(.width(32)) adder_2 (.a(PC), .b(bit_extender_6_out), .out(out_8));  // open: cin, cout
  Adder #(.width(32)) adder_3 (.a(PC), .b(shifter_2_out), .out(out_7));  // open: cin, cout

  assign out_9 = out_4;

  // Notes on the sheet:
  //   I type
  //   S type
  //   SB type
  //   U type
  //   UJ type
endmodule

module control_unit (
  input  [6:0] in_1,
  output MEM_write,
  output Branch,
  output MEMREAD,
  output Reg_write,
  output out_6,
  output [1:0] PcSelect,
  output out_8,
  output out_9,
  output out_10,
  output out_11
);

  wire opcode_decode_1_auipc, opcode_decode_1_branch, opcode_decode_1_i_type, opcode_decode_1_jal,
       opcode_decode_1_jalr, opcode_decode_1_load, opcode_decode_1_lui, opcode_decode_1_r_format,
       opcode_decode_1_store;

  opcode_decode opcode_decode_1 (
    .opcode(in_1), .R_format(opcode_decode_1_r_format), .Load(opcode_decode_1_load),
    .Store(opcode_decode_1_store), .Branch(opcode_decode_1_branch), .I_Type(opcode_decode_1_i_type),
    .JALR(opcode_decode_1_jalr), .JAL(opcode_decode_1_jal), .Lui(opcode_decode_1_lui),
    .auipc(opcode_decode_1_auipc));
  control_decode control_decode_1 (
    .s(opcode_decode_1_store), .B(opcode_decode_1_branch), .r(opcode_decode_1_r_format),
    .l(opcode_decode_1_load), .MEM_write(MEM_write), .Branch(Branch), .MEMREAD(MEMREAD),
    .Reg_write(Reg_write), .out_14(out_6), .i(opcode_decode_1_i_type), .out_15(PcSelect),
    .j(opcode_decode_1_jal), .jr(opcode_decode_1_jalr), .lui(opcode_decode_1_lui), .out_16(out_8),
    .auipc(opcode_decode_1_auipc), .out_17(out_9), .out_18(out_10), .out_19(out_11));

  // Notes on the sheet:
  //   MEM to Reg
endmodule

module opcode_decode (
  input  [6:0] opcode,
  output R_format,
  output Load,
  output Store,
  output Branch,
  output I_Type,
  output JALR,
  output JAL,
  output Lui,
  output auipc
);

  Comparator #(.width(7), .mode("unsigned")) comparator_1 (.a(7'b0110011), .b(opcode), .eq(R_format));  // open: gt, lt
  Comparator #(.width(7), .mode("unsigned")) comparator_2 (.a(opcode), .b(7'b0000011), .eq(Load));  // open: gt, lt
  Comparator #(.width(7), .mode("unsigned")) comparator_3 (.a(opcode), .b(7'b0100011), .eq(Store));  // open: gt, lt
  Comparator #(.width(7), .mode("unsigned")) comparator_4 (.a(opcode), .b(7'b1100011), .eq(Branch));  // open: gt, lt
  Comparator #(.width(7), .mode("unsigned")) comparator_5 (.a(opcode), .b(7'b0010011), .eq(I_Type));  // open: gt, lt
  Comparator #(.width(7), .mode("unsigned")) comparator_6 (.a(opcode), .b(7'b1100111), .eq(JALR));  // open: gt, lt
  Comparator #(.width(7), .mode("unsigned")) comparator_7 (.a(opcode), .b(7'b1101111), .eq(JAL));  // open: gt, lt
  Comparator #(.width(7), .mode("unsigned")) comparator_8 (.a(opcode), .b(7'b0110111), .eq(Lui));  // open: gt, lt
  Comparator #(.width(7), .mode("unsigned")) comparator_9 (.a(opcode), .b(7'b0010111), .eq(auipc));  // open: gt, lt
endmodule

module imediate_select (
  input  [31:0] in_1,
  input  [31:0] in_2,
  input  [6:0] in_3,
  output [31:0] out_4,
  output [4:0] out_5,
  output out_6,
  output [31:0] out_7,
  output [31:0] out_8
);

  wire comparator_1_eq, opcode_decode_1_auipc, opcode_decode_1_i_type, opcode_decode_1_jalr,
       opcode_decode_1_load;
  wire [31:0] imediate_generator_1_out_3, imediate_generator_1_out_4, imediate_generator_1_out_5,
       imediate_generator_1_out_6, imediate_generator_1_out_8, multiplexer_1_out;

  opcode_decode opcode_decode_1 (
    .opcode(in_3), .Load(opcode_decode_1_load), .Store(out_5[1]), .Branch(out_5[2]),
    .I_Type(opcode_decode_1_i_type), .JALR(opcode_decode_1_jalr), .JAL(out_5[4]), .Lui(out_5[3]),
    .auipc(opcode_decode_1_auipc));  // open: R_format
  Imediate_generator imediate_generator_1 (
    .in_1(in_1), .out_3(imediate_generator_1_out_3), .out_4(imediate_generator_1_out_4),
    .out_5(imediate_generator_1_out_5), .out_6(imediate_generator_1_out_6),
    .out_8(imediate_generator_1_out_8), .PC(in_2), .out_7(out_7), .out_9(out_8));
  Comparator #(.width(7), .mode("unsigned")) comparator_1 (
    .a(in_3), .b(7'b1101111), .eq(comparator_1_eq));  // open: gt, lt
  or or_1 (out_5[0], opcode_decode_1_load, opcode_decode_1_i_type);
  or or_2 (out_6, opcode_decode_1_load, out_5[1], out_5[2], opcode_decode_1_i_type, opcode_decode_1_jalr, out_5[4], out_5[3], opcode_decode_1_auipc);
  Multiplexer #(.select(5), .width(32)) multiplexer_1 (
    .in0({32{1'b0}}), .in1(imediate_generator_1_out_3), .in2(imediate_generator_1_out_4),
    .in4(imediate_generator_1_out_5), .in8(imediate_generator_1_out_6), .out(multiplexer_1_out), .sel(out_5));  // open: in3, in5, in6, in7, in9, in10, in11, in12, in13, in14, in15, in16, in17, in18, in19, in20, in21, in22, in23, in24, in25, in26, in27, in28, in29, in30, in31, en
  Multiplexer #(.width(32), .enable("false")) multiplexer_2 (
    .in0(multiplexer_1_out), .in1(imediate_generator_1_out_8), .out(out_4), .sel(comparator_1_eq));
endmodule

module control_decode (
  input  s,
  input  B,
  input  r,
  input  l,
  input  i,
  input  j,
  input  jr,
  input  lui,
  input  auipc,
  output MEM_write,
  output Branch,
  output MEMREAD,
  output Reg_write,
  output out_14,
  output [1:0] out_15,
  output out_16,
  output out_17,
  output out_18,
  output out_19
);

  or or_1 (Reg_write, lui, j, r, j, l, jr, i, lui, jr, auipc);
  PcSelect pcselect_1 (.B(B), .J(j), .JR(jr), .out_4(out_15));
  U_UJselector u_ujselector_1 (
    .in_1(lui), .in_2(auipc), .in_3(j), .in_4(jr), .out_5(out_16), .out_6(out_17), .out_7(out_18),
    .out_8(out_19));

  assign Branch = B;
  assign MEM_write = s;
  assign MEMREAD = l;
  assign out_14 = l;

  // Notes on the sheet:
  //   MEM to Reg
endmodule

module RISC_V (
  input  in_1,
  output [1:0] out_2,
  output [31:0] out_3,
  output [23:0] out_4,
  output [31:0] out_5,
  output [31:0] out_6
);

  wire and_1_out, clock_1_out, completealu_1_out_6, control_unit_1_branch, control_unit_1_mem_write,
       control_unit_1_memread, control_unit_1_out_6, control_unit_1_out_8, control_unit_1_out_9,
       control_unit_1_out_10, control_unit_1_reg_write;
  wire [1:0] imediate_select_1_out_6;
  wire [3:0] alu_control_1_out_2;
  wire [6:0] rom_1_data;
  wire [31:0] adder_1_out, imediate_select_1_out_7, imediate_select_1_out_8, multiplexer_1_out,
       multiplexer_2_out, multiplexer_3_out, multiplexer_4_out, multiplexer_5_out, outputcontrol_1_out_10,
       ram_1_data, reg_file_1_out_8, reg_file_1_out_9, register_1_q;
  wire [31:7] rom_1_data_2;

  Multiplexer #(.width(32), .enable("false")) multiplexer_1 (
    .in0(adder_1_out), .in1(out_6), .out(multiplexer_1_out), .sel(and_1_out));
  Multiplexer #(.select(2), .width(32), .enable("false")) multiplexer_2 (
    .in0(adder_1_out), .in1(multiplexer_1_out), .in2(out_6), .in3(outputcontrol_1_out_10),
    .out(multiplexer_2_out), .sel(out_2));
  Register #(.width(32)) register_1 (
    .D(multiplexer_2_out), .Q(register_1_q), .clk(clock_1_out), .clr(in_1));  // open: en
  Adder #(.width(32)) adder_1 (.a(32'h4), .b(register_1_q), .out(adder_1_out));  // open: cin, cout
  Clock clock_1 (.out(clock_1_out));
  control_unit control_unit_1 (
    .in_1(rom_1_data), .MEM_write(control_unit_1_mem_write), .Branch(control_unit_1_branch),
    .MEMREAD(control_unit_1_memread), .Reg_write(control_unit_1_reg_write), .out_6(control_unit_1_out_6),
    .PcSelect(out_2), .out_8(control_unit_1_out_8), .out_9(control_unit_1_out_9),
    .out_10(control_unit_1_out_10), .out_11(imediate_select_1_out_6[1]));
  ROM #(.addrWidth(20), .dataWidth(32)) rom_1 (
    .addr(register_1_q[21:2]), .data({rom_1_data_2, rom_1_data}));  // open: sel
  Multiplexer #(.width(32), .enable("false")) multiplexer_3 (
    .in0(multiplexer_4_out), .in1(adder_1_out), .out(multiplexer_3_out), .sel(imediate_select_1_out_6[1]));
  and and_1 (and_1_out, completealu_1_out_6, control_unit_1_branch);
  Multiplexer #(.width(32), .enable("false")) multiplexer_4 (
    .in0(outputcontrol_1_out_10), .in1(imediate_select_1_out_7), .out(multiplexer_4_out),
    .sel(control_unit_1_out_9));
  imediate_select imediate_select_1 (
    .in_1({rom_1_data_2, rom_1_data}), .in_3(rom_1_data), .out_4(out_6), .out_6(imediate_select_1_out_6[0]),
    .in_2(register_1_q), .out_7(imediate_select_1_out_7), .out_8(imediate_select_1_out_8));  // open: out_5
  Alu_control alu_control_1 (.in_1({rom_1_data_2, rom_1_data}), .out_2(alu_control_1_out_2));
  Reg_file reg_file_1 (
    .write_enable(control_unit_1_reg_write), .out_8(reg_file_1_out_8), .out_9(reg_file_1_out_9),
    .in_1(multiplexer_3_out), .rd(rom_1_data_2[11:7]), .rs1(rom_1_data_2[19:15]), .rs2(rom_1_data_2[24:20]),
    .in_7(in_1), .in_6(clock_1_out));
  outputcontrol outputcontrol_1 (
    .out_10(outputcontrol_1_out_10), .in_2(out_6), .in_4(adder_1_out), .in_9(out_3),
    .in_5(imediate_select_1_out_6[1]), .in_6(control_unit_1_out_10), .in_7(control_unit_1_out_9),
    .in_8(control_unit_1_out_8), .in_1(out_3));  // open: in_3
  CompleteALU completealu_1 (
    .dataA(reg_file_1_out_8), .dataB(multiplexer_5_out), .fun7(alu_control_1_out_2[3]),
    .fun3(alu_control_1_out_2[2:0]), .out_7({out_5[31:26], out_4, out_5[1:0]}), .aluControl(rom_1_data),
    .out_6(completealu_1_out_6));
  Multiplexer #(.select(2), .width(32), .enable("false")) multiplexer_5 (
    .in0(reg_file_1_out_9), .in1(out_6), .in3(imediate_select_1_out_8), .out(multiplexer_5_out),
    .sel(imediate_select_1_out_6));  // open: in2
  Multiplexer #(.width(32), .enable("false")) multiplexer_6 (
    .in0({out_5[31:26], out_4, out_5[1:0]}), .in1(ram_1_data), .out(out_3), .sel(control_unit_1_out_6));
  RAM #(.addrWidth(24), .dataWidth(32), .bus("separate")) ram_1 (
    .addr(out_4), .din(reg_file_1_out_9), .data(ram_1_data), .str(control_unit_1_mem_write),
    .clk(clock_1_out), .ld(control_unit_1_memread), .clr(in_1));  // open: sel

  assign out_5[25:2] = out_4;

  // Notes on the sheet:
  //   contents of rom_1 (hex, n*v repeats v):
  //   1100f13 1e02023 693 613 593 100593 2783 60533 168693 b50633 fed780e3 16f713 fe0706e3 605b3 fe9ff0ef
endmodule

module Alu_control (
  input  [31:0] in_1,
  output [3:0] out_2
);

  wire opcode_decode_1_load, opcode_decode_1_store, or_1_out;

  opcode_decode opcode_decode_1 (
    .opcode(in_1[6:0]), .Load(opcode_decode_1_load), .Store(opcode_decode_1_store));  // open: R_format, Branch, I_Type, JALR, JAL, Lui, auipc
  or or_1 (or_1_out, opcode_decode_1_load, opcode_decode_1_store);
  Multiplexer #(.width(4)) multiplexer_1 (
    .in0({in_1[30], in_1[14:12]}), .in1(4'b0000), .out(out_2), .sel(or_1_out));  // open: en

  // Notes on the sheet:
  //   INST.
endmodule

module PcSelect (
  input  B,
  input  J,
  input  JR,
  output [1:0] out_4
);

  wire and_1_out, and_2_out, and_3_out, and_4_out, not_1_out, not_2_out, not_3_out, not_4_out, not_5_out,
       not_6_out, not_7_out, not_8_out;

  not not_1 (not_1_out, B);
  not not_2 (not_2_out, J);
  not not_3 (not_3_out, B);
  not not_4 (not_4_out, JR);
  not not_5 (not_5_out, B);
  not not_6 (not_6_out, J);
  not not_7 (not_7_out, J);
  not not_8 (not_8_out, JR);
  and and_1 (and_1_out, not_1_out, not_2_out, JR);
  and and_2 (and_2_out, not_3_out, J, not_4_out);
  and and_3 (and_3_out, not_5_out, not_6_out, JR);
  and and_4 (and_4_out, B, not_7_out, not_8_out);
  or or_1 (out_4[1], and_1_out, and_2_out);
  or or_2 (out_4[0], and_3_out, and_4_out);

  // Notes on the sheet:
  //   pc select
endmodule

module alu (
  input  [31:0] in_1,
  input  [31:0] in_2,
  input  in_3,
  input  [2:0] in_4,
  output [31:0] out_5
);

  wire comparator_1_lt, comparator_2_lt;
  wire [31:0] adder_1_out, and_1_out, multiplexer_1_out, multiplexer_2_out, multiplexer_3_out,
       multiplexer_4_out, or_1_out, shifter_1_out, shifter_2_out, shifter_3_out, subtractor_1_out, xor_1_out;

  Adder #(.width(32)) adder_1 (.a(in_1), .b(in_2), .out(adder_1_out));  // open: cin, cout
  Subtractor #(.width(32)) subtractor_1 (.a(in_1), .b(in_2), .out(subtractor_1_out));  // open: bin, bout
  Shifter #(.width(32)) shifter_1 (.in(in_1), .\dist (in_2[4:0]), .out(shifter_1_out));
  Comparator #(.width(32)) comparator_1 (.a(in_1), .b(in_2), .lt(comparator_1_lt));  // open: gt, eq
  Comparator #(.width(32), .mode("unsigned")) comparator_2 (.a(in_1), .b(in_2), .lt(comparator_2_lt));  // open: gt, eq
  assign xor_1_out = in_1 ^ in_2;  // XOR_Gate xor_1, 32 bits wide
  Shifter #(.width(32), .shift("lr")) shifter_2 (.in(in_1), .\dist (in_2[4:0]), .out(shifter_2_out));
  Shifter #(.width(32), .shift("ar")) shifter_3 (.in(in_1), .\dist (in_2[4:0]), .out(shifter_3_out));
  assign or_1_out = in_1 | in_2;  // OR_Gate or_1, 32 bits wide
  assign and_1_out = in_1 & in_2;  // AND_Gate and_1, 32 bits wide
  Multiplexer #(.width(32)) multiplexer_1 (
    .in0(adder_1_out), .in1(subtractor_1_out), .out(multiplexer_1_out), .sel(in_3));  // open: en
  Multiplexer #(.width(32)) multiplexer_2 (
    .in0(shifter_2_out), .in1(shifter_3_out), .out(multiplexer_2_out), .sel(in_3));  // open: en
  Multiplexer #(.width(32)) multiplexer_3 (
    .in0({32{1'b0}}), .in1(32'h1), .out(multiplexer_3_out), .sel(comparator_1_lt));  // open: en
  Multiplexer #(.width(32)) multiplexer_4 (
    .in0({32{1'b0}}), .in1(32'h1), .out(multiplexer_4_out), .sel(comparator_2_lt));  // open: en
  Multiplexer #(.select(3), .width(32)) multiplexer_5 (
    .in0(multiplexer_1_out), .in1(shifter_1_out), .in2(multiplexer_3_out), .in3(multiplexer_4_out),
    .in4(xor_1_out), .in5(multiplexer_2_out), .in6(or_1_out), .in7(and_1_out), .out(out_5), .sel(in_4));  // open: en

  // Notes on the sheet:
  //   ALU
endmodule

module CompleteALU (
  input  [31:0] dataA,
  input  [31:0] dataB,
  input  fun7,
  input  [2:0] fun3,
  input  [6:0] aluControl,
  output out_6,
  output [31:0] out_7
);

  wire comparator_1_eq, comparator_2_eq, comparator_2_gt, comparator_2_lt, comparator_3_eq, comparator_3_gt,
       comparator_3_lt, comparator_4_eq, not_1_out, opcode_decode_1_branch, or_1_out, or_2_out;
  wire [31:0] alu_1_out_5, multiplexer_1_out, multiplexer_2_out, multiplexer_3_out, multiplexer_4_out,
       multiplexer_5_out, multiplexer_7_out, multiplexer_8_out;

  opcode_decode opcode_decode_1 (
    .opcode(aluControl), .Branch(opcode_decode_1_branch));  // open: R_format, Load, Store, I_Type, JALR, JAL, Lui, auipc
  Comparator #(.width(32)) comparator_1 (.a(dataA), .b(dataB), .eq(comparator_1_eq));  // open: gt, lt
  Comparator #(.width(32), .mode("unsigned")) comparator_2 (
    .a(dataA), .b(dataB), .gt(comparator_2_gt), .eq(comparator_2_eq), .lt(comparator_2_lt));
  alu alu_1 (.in_1(dataA), .in_2(dataB), .out_5(alu_1_out_5), .in_3(fun7), .in_4(fun3));
  Multiplexer #(.width(32), .enable("false")) multiplexer_1 (
    .in0({32{1'b0}}), .in1(32'h1), .out(multiplexer_1_out), .sel(comparator_3_eq));
  Comparator #(.width(32)) comparator_3 (
    .a(dataA), .b(dataB), .gt(comparator_3_gt), .eq(comparator_3_eq), .lt(comparator_3_lt));
  Multiplexer #(.width(32), .enable("false")) multiplexer_2 (
    .in0({32{1'b0}}), .in1(32'h1), .out(multiplexer_2_out), .sel(comparator_3_lt));
  Multiplexer #(.width(32), .enable("false")) multiplexer_3 (
    .in0({32{1'b0}}), .in1(32'h1), .out(multiplexer_3_out), .sel(or_1_out));
  or or_1 (or_1_out, comparator_3_gt, comparator_3_eq);
  not not_1 (not_1_out, comparator_1_eq);
  or or_2 (or_2_out, comparator_2_gt, comparator_2_eq);
  Multiplexer #(.width(32), .enable("false")) multiplexer_4 (
    .in0({32{1'b0}}), .in1(32'h1), .out(multiplexer_4_out), .sel(not_1_out));
  Multiplexer #(.width(32), .enable("false")) multiplexer_5 (
    .in0({32{1'b0}}), .in1(32'h1), .out(multiplexer_5_out), .sel(comparator_2_lt));
  Multiplexer #(.width(32), .enable("false")) multiplexer_6 (
    .in0(alu_1_out_5), .in1(multiplexer_7_out), .out(out_7), .sel(opcode_decode_1_branch));
  Multiplexer #(.select(3), .width(32), .enable("false")) multiplexer_7 (
    .in0(multiplexer_1_out), .in1(multiplexer_4_out), .in2(multiplexer_2_out), .in3(multiplexer_3_out),
    .in4(multiplexer_5_out), .in5(multiplexer_8_out), .out(multiplexer_7_out), .sel(fun3));  // open: in6, in7
  Multiplexer #(.width(32), .enable("false")) multiplexer_8 (
    .in0({32{1'b0}}), .in1(32'h1), .out(multiplexer_8_out), .sel(or_2_out));
  Comparator #(.width(32), .mode("unsigned")) comparator_4 (
    .a(out_7), .b(32'h1), .eq(comparator_4_eq));  // open: gt, lt
  and and_1 (out_6, opcode_decode_1_branch, comparator_4_eq);

  // Notes on the sheet:
  //   blt
  //   bge
  //   R, I, L, S TYPE ALU
  //   beq
  //   bne
  //   bltu
  //   bgeu
  //   BRANCH
endmodule

module U_UJselector (
  input  in_1,
  input  in_2,
  input  in_3,
  input  in_4,
  output out_5,
  output out_6,
  output out_7,
  output out_8
);


  assign out_5 = in_1;
  assign out_6 = in_2;
  assign out_7 = in_3;
  assign out_8 = in_4;
endmodule

module outputcontrol (
  input  [31:0] in_1,
  input  [31:0] in_2,
  input  [31:0] in_3,
  input  [31:0] in_4,
  input  in_5,
  input  in_6,
  input  in_7,
  input  in_8,
  input  [31:0] in_9,
  output [31:0] out_10
);

  Multiplexer #(.select(4), .width(32), .enable("false")) multiplexer_1 (
    .in0(in_1), .in1(in_2), .in2(in_3), .in4(in_4), .in8(in_9), .out(out_10), .sel({in_5, in_6, in_7, in_8}));  // open: in3, in5, in6, in7, in9, in10, in11, in12, in13, in14, in15
endmodule
