// Logisim project RV32I.circ as structural Verilog: 3 circuits, main circuit main
module main (
  input  in_1,
  output [31:0] out_2
);

  wire clock_1_out;
  wire [31:0] adder_1_out, register_1_q;

  Clock clock_1 (.out(clock_1_out));
  Register #(.width(32)) register_1 (.D(adder_1_out), .Q(register_1_q), .clk(clock_1_out), .clr(in_1));  // open: en
  Adder #(.width(32)) adder_1 (.a(32'h4), .b(register_1_q), .out(adder_1_out));  // open: cin, cout
  ROM #(.addrWidth(20), .dataWidth(32)) rom_1 (.addr(register_1_q[21:2]), .data(out_2));  // open: sel

  // Notes on the sheet:
  //   FETCH UNIT
  //   contents of rom_1 (hex, n*v repeats v):
  //   11111111
endmodule

module ALU (
  input  [31:0] in_1,
  input  [31:0] in_2,
  input  in_3,
  input  [2:0] in_4,
  output [31:0] out_5
);

  wire comparator_1_lt, comparator_2_lt;
  wire [31:0] adder_1_out, and_1_out, multiplexer_1_out, multiplexer_2_out, multiplexer_3_out,
       multiplexer_4_out, or_1_out, shifter_1_out, shifter_2_out, shifter_3_out, subtractor_1_out, xor_1_out;

  Adder #(.width(32)) adder_1 (.a(in_1), .b(in_2), .out(adder_1_out));  // open: cin, cout
  Subtractor #(.width(32)) subtractor_1 (.a(in_1), .b(in_2), .out(subtractor_1_out));  // open: bin, bout
  Shifter #(.width(32)) shifter_1 (.in(in_1), .\dist (in_2[4:0]), .out(shifter_1_out));
  Comparator #(.width(32)) comparator_1 (.a(in_1), .b(in_2), .lt(comparator_1_lt));  // open: gt, eq
  Comparator #(.width(32), .mode("unsigned")) comparator_2 (.a(in_1), .b(in_2), .lt(comparator_2_lt));  // open: gt, eq
  assign xor_1_out = in_1 ^ in_2;  // XOR_Gate xor_1, 32 bits wide
  Shifter #(.width(32), .shift("lr")) shifter_2 (.in(in_1), .\dist (in_2[4:0]), .out(shifter_2_out));
  Shifter #(.width(32), .shift("ar")) shifter_3 (.in(in_1), .\dist (in_2[4:0]), .out(shifter_3_out));
  assign or_1_out = in_1 | in_2;  // OR_Gate or_1, 32 bits wide
  assign and_1_out = in_1 & in_2;  // AND_Gate and_1, 32 bits wide
  Multiplexer #(.width(32)) multiplexer_1 (
    .in0(adder_1_out), .in1(subtractor_1_out), .out(multiplexer_1_out), .sel(in_3));  // open: en
  Multiplexer #(.width(32)) multiplexer_2 (
    .in0(shifter_2_out), .in1(shifter_3_out), .out(multiplexer_2_out), .sel(in_3));  // open: en
  Multiplexer #(.width(32)) multiplexer_3 (
    .in0({32{1'b0}}), .in1(32'h1), .out(multiplexer_3_out), .sel(comparator_1_lt));  // open: en
  Multiplexer #(.width(32)) multiplexer_4 (
    .in0({32{1'b0}}), .in1(32'h1), .out(multiplexer_4_out), .sel(comparator_2_lt));  // open: en
  Multiplexer #(.select(3), .width(32)) multiplexer_5 (
    .in0(multiplexer_1_out), .in1(shifter_1_out), .in2(multiplexer_3_out), .in3(multiplexer_4_out),
    .in4(xor_1_out), .in5(multiplexer_2_out), .in6(or_1_out), .in7(and_1_out), .out(out_5), .sel(in_4));  // open: en

  // Notes on the sheet:
  //   ALU
endmodule

module PC (
  input  in_1,
  output [31:0] out_2
);

  wire clock_1_out;
  wire [31:0] adder_1_out, register_1_q;

  Clock clock_1 (.out(clock_1_out));
  Register #(.width(32)) register_1 (.D(adder_1_out), .Q(register_1_q), .clk(clock_1_out), .clr(in_1));  // open: en
  Adder #(.width(32)) adder_1 (.a(32'h4), .b(register_1_q), .out(adder_1_out));  // open: cin, cout
  ROM #(.addrWidth(20), .dataWidth(32)) rom_1 (.addr(register_1_q[21:2]), .data(out_2));  // open: sel

  // Notes on the sheet:
  //   FETCH UNIT
  //   contents of rom_1 (hex, n*v repeats v):
  //   11111111
endmodule
